// Logisim project Lab_1.circ as structural Verilog: 13 circuits, main circuit main
module main (
  input  RESET,
  input  RUN_SYSTEM,
  output [4:0] out_3,
  output [4:0] out_4,
  output [7:0] out_5,
  output [4:0] out_6,
  output [4:0] out_7,
  output out_8,
  output [7:0] out_9,
  output [7:0] out_10,
  output [7:0] out_11
);

  wire and_4_out, BIT_RAM, CLK_1, CLK_1_out, CLK_2, CLK_2_out, comparador_8bits_1_igual,
       comparador_8bits_1_mayor, COMPARATE, d_ff_1_q, display_1_a1, display_1_a10, display_1_a100,
       display_1_b1, display_1_b10, display_1_b100, display_1_c1, display_1_c10, display_1_c100,
       display_1_d1, display_1_d10, display_1_d100, display_1_e1, display_1_e10, display_1_e100,
       display_1_f1, display_1_f10, display_1_f100, display_1_g1, display_1_g10, display_1_g100,
       display_2_a1, display_2_a10, display_2_a100, display_2_b1, display_2_b10, display_2_b100,
       display_2_c1, display_2_c10, display_2_c100, display_2_d1, display_2_d10, display_2_d100,
       display_2_e1, display_2_e10, display_2_e100, display_2_f1, display_2_f10, display_2_f100,
       display_2_g1, display_2_g10, display_2_g100, display_3_a1, display_3_a10, display_3_a100,
       display_3_b1, display_3_b10, display_3_b100, display_3_c1, display_3_c10, display_3_c100,
       display_3_d1, display_3_d10, display_3_d100, display_3_e1, display_3_e10, display_3_e100,
       display_3_f1, display_3_f10, display_3_f100, display_3_g1, display_3_g10, display_3_g100, ESTADO_0,
       mef_1_e0, mef_1_e2, mef_1_e4, not_1_out, or_1_out, Register_A, Register_B, WE;
  wire [4:0] multiplexer_1_out;

  Clock u_CLK_1 (.out(CLK_1_out));
  Clock #(.highDuration(2), .lowDuration(2)) u_CLK_2 (.out(CLK_2_out));
  and and_1 (CLK_1, CLK_1_out, RUN_SYSTEM);
  and and_2 (CLK_2, CLK_2_out, RUN_SYSTEM);
  MEF mef_1 (
    .CLK(CLK_1), .RESET(RESET), .E0(mef_1_e0), .E1(ESTADO_0), .E2(mef_1_e2), .E3(Register_A), .E4(mef_1_e4),
    .E5(Register_B), .E6(COMPARATE), .E7(WE));
  not not_1 (not_1_out, mef_1_e2);
  and and_3 (BIT_RAM, not_1_out, mef_1_e4);
  and and_4 (and_4_out, d_ff_1_q, ESTADO_0);
  Multiplexer #(.width(5)) multiplexer_1 (.in0(out_7), .in1(out_6), .out(multiplexer_1_out), .sel(BIT_RAM));
  RAM #(.addrWidth(5), .trigger("high")) ram_1 (
    .addr(multiplexer_1_out), .we(WE), .oe(1'b1), .din(out_5), .dout(out_11));
  contador_mascara contador_mascara_1 (
    .CLK(CLK_2), .RUN(mef_1_e0), .RESET(RESET), .RUN_2(and_4_out), .A(out_7), .B(out_6), .MASK(out_3),
    .NUM_SUM(out_4));
  D_Flip_Flop d_ff_1 (.D(out_8), .clk(CLK_1), .Q(d_ff_1_q), .reset(RESET));  // open: Qn, preset
  Comparator #(.width(5)) comparator_1 (.a(out_4), .b(out_6), .eq(out_8));  // open: gt, lt
  Display display_1 (
    .in_1(out_10), .A100(display_1_a100), .B100(display_1_b100), .C100(display_1_c100),
    .D100(display_1_d100), .E100(display_1_e100), .F100(display_1_f100), .G100(display_1_g100),
    .A10(display_1_a10), .B10(display_1_b10), .C10(display_1_c10), .D10(display_1_d10), .E10(display_1_e10),
    .F10(display_1_f10), .G10(display_1_g10), .A1(display_1_a1), .B1(display_1_b1), .C1(display_1_c1),
    .D1(display_1_d1), .E1(display_1_e1), .F1(display_1_f1), .G1(display_1_g1));
  Display display_2 (
    .in_1(out_9), .A100(display_2_a100), .B100(display_2_b100), .C100(display_2_c100), .D100(display_2_d100),
    .E100(display_2_e100), .F100(display_2_f100), .G100(display_2_g100), .A10(display_2_a10),
    .B10(display_2_b10), .C10(display_2_c10), .D10(display_2_d10), .E10(display_2_e10), .F10(display_2_f10),
    .G10(display_2_g10), .A1(display_2_a1), .B1(display_2_b1), .C1(display_2_c1), .D1(display_2_d1),
    .E1(display_2_e1), .F1(display_2_f1), .G1(display_2_g1));
  Register register_1 (.D(out_11), .en(1'b1), .clk(Register_A), .Q(out_9), .clr(RESET));
  Register register_2 (.D(out_11), .en(1'b1), .clk(Register_B), .Q(out_10), .clr(RESET));
  _7_Segment_Display u_7_segment_display_1 (
    .g(display_1_g100), .f(display_1_f100), .a(display_1_a100), .b(display_1_b100), .e(display_1_e100),
    .d(display_1_d100), .c(display_1_c100));  // open: dp
  _7_Segment_Display u_7_segment_display_2 (
    .g(display_1_g10), .f(display_1_f10), .a(display_1_a10), .b(display_1_b10), .e(display_1_e10),
    .d(display_1_d10), .c(display_1_c10));  // open: dp
  _7_Segment_Display u_7_segment_display_3 (
    .g(display_1_g1), .f(display_1_f1), .a(display_1_a1), .b(display_1_b1), .e(display_1_e1),
    .d(display_1_d1), .c(display_1_c1));  // open: dp
  comparador_8bits comparador_8bits_1 (
    .A(out_9), .B(out_10), .MAYOR(comparador_8bits_1_mayor), .IGUAL(comparador_8bits_1_igual));  // open: MENOR
  _7_Segment_Display u_7_segment_display_4 (
    .g(display_2_g100), .f(display_2_f100), .a(display_2_a100), .b(display_2_b100), .e(display_2_e100),
    .d(display_2_d100), .c(display_2_c100));  // open: dp
  _7_Segment_Display u_7_segment_display_5 (
    .g(display_2_g10), .f(display_2_f10), .a(display_2_a10), .b(display_2_b10), .e(display_2_e10),
    .d(display_2_d10), .c(display_2_c10));  // open: dp
  or or_1 (or_1_out, comparador_8bits_1_mayor, comparador_8bits_1_igual);
  _7_Segment_Display u_7_segment_display_6 (
    .g(display_2_g1), .f(display_2_f1), .a(display_2_a1), .b(display_2_b1), .e(display_2_e1),
    .d(display_2_d1), .c(display_2_c1));  // open: dp
  Multiplexer #(.width(8)) multiplexer_2 (.in0(out_9), .in1(out_10), .out(out_5), .sel(or_1_out));
  Display display_3 (
    .in_1(out_5), .A100(display_3_a100), .B100(display_3_b100), .C100(display_3_c100), .D100(display_3_d100),
    .E100(display_3_e100), .F100(display_3_f100), .G100(display_3_g100), .A10(display_3_a10),
    .B10(display_3_b10), .C10(display_3_c10), .D10(display_3_d10), .E10(display_3_e10), .F10(display_3_f10),
    .G10(display_3_g10), .A1(display_3_a1), .B1(display_3_b1), .C1(display_3_c1), .D1(display_3_d1),
    .E1(display_3_e1), .F1(display_3_f1), .G1(display_3_g1));
  _7_Segment_Display u_7_segment_display_7 (
    .g(display_3_g100), .f(display_3_f100), .a(display_3_a100), .b(display_3_b100), .e(display_3_e100),
    .d(display_3_d100), .c(display_3_c100));  // open: dp
  _7_Segment_Display u_7_segment_display_8 (
    .g(display_3_g10), .f(display_3_f10), .a(display_3_a10), .b(display_3_b10), .e(display_3_e10),
    .d(display_3_d10), .c(display_3_c10));  // open: dp
  _7_Segment_Display u_7_segment_display_9 (
    .g(display_3_g1), .f(display_3_f1), .a(display_3_a1), .b(display_3_b1), .e(display_3_e1),
    .d(display_3_d1), .c(display_3_c1));  // open: dp

  // Other names for the same wires on the sheet: A[4:0] = out_7; B[4:0] = out_6; DATA_SAVE[7:0] = out_5
endmodule

module comparador_2bits (
  input  [1:0] A,
  input  [1:0] B,
  output AmyB,
  output AigB,
  output AmnB
);

  wire and_1_out, and_2_out, and_3_out, and_4_out, and_5_out, and_6_out, and_7_out, and_8_out, and_9_out,
       and_10_out, not_1_out, not_2_out, not_3_out, not_4_out;

  not not_1 (not_1_out, A[1]);
  not not_2 (not_2_out, A[0]);
  not not_3 (not_3_out, B[1]);
  not not_4 (not_4_out, B[0]);
  and and_1 (and_1_out, A[1], not_3_out);
  and and_2 (and_2_out, A[1], A[0], not_4_out);
  and and_3 (and_3_out, A[0], not_3_out, not_4_out);
  and and_4 (and_4_out, not_1_out, not_2_out, not_3_out, not_4_out);
  and and_5 (and_5_out, not_1_out, A[0], not_3_out, B[0]);
  and and_6 (and_6_out, A[1], A[0], B[1], B[0]);
  and and_7 (and_7_out, A[1], not_2_out, B[1], not_4_out);
  and and_8 (and_8_out, not_1_out, B[1]);
  and and_9 (and_9_out, not_1_out, not_2_out, B[0]);
  and and_10 (and_10_out, not_1_out, not_2_out, B[0]);
  or or_1 (AmyB, and_1_out, and_2_out, and_3_out);
  or or_2 (AigB, and_4_out, and_5_out, and_6_out, and_7_out);
  or or_3 (AmnB, and_8_out, and_9_out, and_10_out);
endmodule

module comparador_4bits (
  input  [3:0] A,
  input  [3:0] B,
  output out_3,
  output out_4,
  output out_5
);

  wire [2:0] comparador_2bits_1_amyb, comparador_2bits_2_amyb;

  comparador_2bits comparador_2bits_1 (
    .A(A[3:2]), .B(B[3:2]), .AmyB(comparador_2bits_1_amyb[0]), .AigB(comparador_2bits_1_amyb[1]),
    .AmnB(comparador_2bits_1_amyb[2]));
  comparador_2bits comparador_2bits_2 (
    .A(A[1:0]), .B(B[1:0]), .AmyB(comparador_2bits_2_amyb[0]), .AigB(comparador_2bits_2_amyb[1]),
    .AmnB(comparador_2bits_2_amyb[2]));
  comparador comparador_1 (
    .MasS(comparador_2bits_1_amyb), .MenosS(comparador_2bits_2_amyb), .mayor(out_3), .igual(out_4),
    .menor(out_5));
endmodule

module comparador_8bits (
  input  [7:0] A,
  input  [7:0] B,
  output MAYOR,
  output IGUAL,
  output MENOR
);

  wire [2:0] comparador_4bits_1_out_3, comparador_4bits_2_out_3;

  comparador_4bits comparador_4bits_1 (
    .A(A[7:4]), .B(B[7:4]), .out_3(comparador_4bits_1_out_3[0]), .out_4(comparador_4bits_1_out_3[1]),
    .out_5(comparador_4bits_1_out_3[2]));
  comparador_4bits comparador_4bits_2 (
    .A(A[3:0]), .B(B[3:0]), .out_3(comparador_4bits_2_out_3[0]), .out_4(comparador_4bits_2_out_3[1]),
    .out_5(comparador_4bits_2_out_3[2]));
  comparador comparador_1 (
    .MasS(comparador_4bits_1_out_3), .MenosS(comparador_4bits_2_out_3), .mayor(MAYOR), .igual(IGUAL),
    .menor(MENOR));
endmodule

module comparador (
  input  [2:0] MasS,
  input  [2:0] MenosS,
  output mayor,
  output igual,
  output menor
);

  wire and_1_out, and_2_out;

  and and_1 (and_1_out, MasS[1], MenosS[0]);
  and and_2 (and_2_out, MasS[1], MenosS[2]);
  or or_1 (mayor, MasS[0], and_1_out);
  and and_3 (igual, MasS[1], MenosS[1]);
  or or_2 (menor, and_2_out, MasS[2]);
endmodule

module contador_de_fase (
  input  Reset,
  input  CLK,
  input  RUN,
  output [4:0] MASK
);

  wire and_1_out, and_2_out, and_3_out, and_4_out, and_5_out, and_6_out, not_1_out, not_2_out, not_3_out,
       not_4_out, not_5_out, not_6_out;

  not not_1 (not_1_out, 1'b1);
  not not_2 (not_2_out, MASK[4]);
  not not_3 (not_3_out, MASK[3]);
  not not_4 (not_4_out, MASK[2]);
  not not_5 (not_5_out, MASK[1]);
  not not_6 (not_6_out, MASK[0]);
  and and_1 (and_1_out, not_2_out, not_3_out, not_4_out, not_5_out, not_6_out);
  and and_2 (and_2_out, not_2_out, MASK[2], MASK[1], MASK[0]);
  and and_3 (and_3_out, not_2_out, not_3_out, MASK[2], MASK[1], MASK[0]);
  and and_4 (and_4_out, not_2_out, not_3_out, not_4_out, MASK[0]);
  and and_5 (and_5_out, not_2_out, not_3_out, not_4_out, not_5_out);
  and and_6 (and_6_out, CLK, RUN);
  J_K_Flip_Flop A (.J(not_1_out), .K(not_1_out), .clk(and_6_out), .Q(MASK[4]), .reset(Reset));  // open: Qn, preset
  J_K_Flip_Flop B (.J(and_1_out), .K(and_2_out), .clk(and_6_out), .Q(MASK[3]), .reset(Reset));  // open: Qn, preset
  J_K_Flip_Flop C (.J(and_1_out), .K(and_3_out), .clk(and_6_out), .Q(MASK[2]), .reset(Reset));  // open: Qn, preset
  J_K_Flip_Flop D (.J(and_1_out), .K(and_4_out), .clk(and_6_out), .Q(MASK[1]), .reset(Reset));  // open: Qn, preset
  J_K_Flip_Flop E (.J(and_5_out), .K(and_5_out), .clk(and_6_out), .Q(MASK[0]), .reset(Reset));  // open: Qn, preset
endmodule

module MEF (
  input  CLK,
  input  RESET,
  output E0,
  output E1,
  output E2,
  output E3,
  output E4,
  output E5,
  output E6,
  output E7
);

  wire and_1_out;
  wire [2:0] FFC_q;

  J_K_Flip_Flop FFA (.J(and_1_out), .K(and_1_out), .clk(CLK), .Q(FFC_q[2]), .reset(RESET));  // open: Qn, preset
  J_K_Flip_Flop FFB (.J(FFC_q[0]), .K(FFC_q[0]), .clk(CLK), .Q(FFC_q[1]), .reset(RESET));  // open: Qn, preset
  J_K_Flip_Flop FFC (.J(1'b1), .K(1'b1), .clk(CLK), .Q(FFC_q[0]), .reset(RESET));  // open: Qn, preset
  and and_1 (and_1_out, FFC_q[1], FFC_q[0]);
  Decoder #(.enable("false"), .select(3)) decoder_1 (
    .out0(E0), .out1(E1), .out2(E2), .out3(E3), .out4(E4), .out5(E5), .out6(E6), .out7(E7), .sel(FFC_q));
endmodule

module contador_mascara (
  input  CLK,
  input  RUN,
  input  RESET,
  input  RUN_2,
  output [4:0] A,
  output [4:0] B,
  output [4:0] MASK,
  output [4:0] NUM_SUM
);

  wire not_1_out, not_2_out, not_3_out;
  wire [4:0] contador_5bits_1_out_4;

  not not_1 (not_1_out, CLK);
  not not_2 (not_2_out, CLK);
  not not_3 (not_3_out, CLK);
  CONTADOR_5BITS contador_5bits_1 (.CLK(not_1_out), .RUN(RUN), .RESET(RESET), .out_4(contador_5bits_1_out_4));
  contador_de_fase contador_de_fase_1 (.Reset(RESET), .CLK(not_2_out), .RUN(RUN_2), .MASK(MASK));
  suma_de_Fase suma_de_fase_1 (.RESET(RESET), .CLK(not_3_out), .RUN(RUN_2), .NUM_SUM(NUM_SUM));
  assign A = contador_5bits_1_out_4 & MASK;  // AND_Gate and_1, 5 bits wide
  assign B = A | NUM_SUM;  // OR_Gate or_1, 5 bits wide
endmodule

module CONTADOR_5BITS (
  input  CLK,
  input  RUN,
  input  RESET,
  output [4:0] out_4
);

  wire and_1_out, and_2_out, and_3_out, and_4_out, and_5_out, and_6_out, and_7_out, and_8_out, and_9_out,
       and_10_out, and_11_out, and_12_out, and_13_out, and_14_out, not_1_out, not_2_out, not_3_out,
       not_4_out, not_5_out, or_1_out, or_2_out, or_3_out, or_4_out;

  and and_1 (and_1_out, CLK, RUN);
  not not_1 (not_1_out, out_4[3]);
  not not_2 (not_2_out, out_4[2]);
  not not_3 (not_3_out, out_4[1]);
  not not_4 (not_4_out, out_4[2]);
  not not_5 (not_5_out, out_4[0]);
  and and_2 (and_2_out, out_4[0], out_4[1], out_4[2], not_1_out);
  and and_3 (and_3_out, out_4[0], out_4[1], out_4[2], out_4[3]);
  and and_4 (and_4_out, out_4[0], out_4[1], out_4[2], out_4[3]);
  and and_5 (and_5_out, out_4[0], out_4[1], out_4[2]);
  and and_6 (and_6_out, out_4[0], out_4[1], not_2_out);
  and and_7 (and_7_out, not_3_out, not_4_out, out_4[0]);
  and and_8 (and_8_out, not_4_out, out_4[1], out_4[0]);
  and and_9 (and_9_out, out_4[2], not_3_out, out_4[0]);
  and and_10 (and_10_out, out_4[2], out_4[1], out_4[0]);
  and and_11 (and_11_out, out_4[1], not_5_out);
  and and_12 (and_12_out, not_5_out, not_3_out);
  and and_13 (and_13_out, out_4[0], out_4[2]);
  and and_14 (and_14_out, out_4[0], not_4_out);
  or or_1 (or_1_out, and_7_out, and_9_out);
  or or_2 (or_2_out, and_8_out, and_10_out);
  or or_3 (or_3_out, and_11_out, and_12_out);
  or or_4 (or_4_out, and_13_out, and_14_out);
  J_K_Flip_Flop A (.J(and_4_out), .K(and_4_out), .clk(and_1_out), .Q(out_4[4]), .reset(RESET));  // open: Qn, preset
  J_K_Flip_Flop B (.J(and_2_out), .K(and_3_out), .clk(and_1_out), .Q(out_4[3]), .reset(RESET));  // open: Qn, preset
  J_K_Flip_Flop C (.J(and_6_out), .K(and_5_out), .clk(and_1_out), .Q(out_4[2]), .reset(RESET));  // open: Qn, preset
  J_K_Flip_Flop D (.J(or_1_out), .K(or_2_out), .clk(and_1_out), .Q(out_4[1]), .reset(RESET));  // open: Qn, preset
  J_K_Flip_Flop E (.J(or_3_out), .K(or_4_out), .clk(and_1_out), .Q(out_4[0]), .reset(RESET));  // open: Qn, preset
endmodule

module suma_de_Fase (
  input  RESET,
  input  CLK,
  input  RUN,
  output [4:0] NUM_SUM
);

  wire and_1_out, and_2_out, and_3_out, and_4_out, and_5_out, and_6_out, and_7_out, and_8_out, and_9_out,
       and_10_out, and_11_out, not_1_out, not_2_out, not_3_out, not_4_out, not_5_out;

  not not_1 (not_1_out, NUM_SUM[4]);
  not not_2 (not_2_out, NUM_SUM[3]);
  not not_3 (not_3_out, NUM_SUM[2]);
  not not_4 (not_4_out, NUM_SUM[1]);
  not not_5 (not_5_out, NUM_SUM[0]);
  and and_1 (and_1_out, CLK, RUN);
  and and_2 (and_2_out, not_1_out, not_2_out, not_3_out, not_4_out);
  and and_3 (and_3_out, not_2_out, not_3_out, not_4_out, not_5_out);
  and and_4 (and_4_out, NUM_SUM[4], not_2_out, not_3_out, not_4_out, not_5_out);
  and and_5 (and_5_out, not_1_out, not_3_out, not_4_out, not_5_out);
  and and_6 (and_6_out, not_1_out, NUM_SUM[3], not_3_out, not_4_out, not_5_out);
  and and_7 (and_7_out, not_1_out, not_2_out, not_4_out, not_5_out);
  and and_8 (and_8_out, not_1_out, not_2_out, NUM_SUM[2], not_4_out, not_5_out);
  and and_9 (and_9_out, not_1_out, not_2_out, not_3_out, NUM_SUM[1], not_5_out);
  and and_10 (and_10_out, not_1_out, not_2_out, not_3_out, NUM_SUM[1], not_5_out);
  and and_11 (and_11_out, not_1_out, not_2_out, not_3_out, not_4_out);
  J_K_Flip_Flop SA (.J(and_2_out), .K(and_3_out), .clk(and_1_out), .Q(NUM_SUM[4]), .reset(RESET));  // open: Qn, preset
  J_K_Flip_Flop SB (.J(and_4_out), .K(and_5_out), .clk(and_1_out), .Q(NUM_SUM[3]), .reset(RESET));  // open: Qn, preset
  J_K_Flip_Flop SC (.J(and_6_out), .K(and_7_out), .clk(and_1_out), .Q(NUM_SUM[2]), .reset(RESET));  // open: Qn, preset
  J_K_Flip_Flop SD (.J(and_8_out), .K(and_9_out), .clk(and_1_out), .Q(NUM_SUM[1]), .reset(RESET));  // open: Qn, preset
  J_K_Flip_Flop SE (
    .J(and_10_out), .K(and_11_out), .clk(and_1_out), .Q(NUM_SUM[0]), .reset(RESET));  // open: Qn, preset
endmodule

module Display (
  input  [7:0] in_1,
  output A100,
  output B100,
  output C100,
  output D100,
  output E100,
  output F100,
  output G100,
  output A10,
  output B10,
  output C10,
  output D10,
  output E10,
  output F10,
  output G10,
  output A1,
  output B1,
  output C1,
  output D1,
  output E1,
  output F1,
  output G1
);

  wire binary_to_bcd_converter_1_p2, binary_to_bcd_converter_1_p3, binary_to_bcd_converter_1_p4;

  // Binary_to_BCD_converter #(.binvalue(8)) binary_to_bcd_converter_1: pin names not known; wires that end beside it: in_1, binary_to_bcd_converter_1_p2, binary_to_bcd_converter_1_p3, binary_to_bcd_converter_1_p4
  _7_Segment_Display #(.decimalPoint("false")) u_7_segment_display_1 (
    .g(G100), .f(F100), .a(A100), .b(B100), .e(E100), .d(D100), .c(C100));
  // BCD_to_7_Segment_decoder bcd_to_7_segment_decoder_1: pin names not known; wires that end beside it: G100, E100, F100, D100, binary_to_bcd_converter_1_p2, A100, C100, B100
  _7_Segment_Display #(.decimalPoint("false")) u_7_segment_display_2 (
    .g(G10), .f(F10), .a(A10), .b(B10), .e(E10), .d(D10), .c(C10));
  // BCD_to_7_Segment_decoder bcd_to_7_segment_decoder_2: pin names not known; wires that end beside it: G10, E10, F10, D10, binary_to_bcd_converter_1_p3, A10, C10, B10
  _7_Segment_Display #(.decimalPoint("false")) u_7_segment_display_3 (
    .g(G1), .f(F1), .a(A1), .b(B1), .e(E1), .d(D1), .c(C1));
  // BCD_to_7_Segment_decoder bcd_to_7_segment_decoder_3: pin names not known; wires that end beside it: G1, E1, F1, D1, binary_to_bcd_converter_1_p4, A1, C1, B1

  // Notes on the sheet:
  //   100
  //   10
  //   1
endmodule

module displayHex (
  input  [7:0] in_1,
  output [3:0] MS,
  output [3:0] LS
);

  Multiplexer #(.select(4), .width(4)) multiplexer_1 (
    .in0(4'b0000), .in1(4'b0001), .in2(4'b0010), .in3(4'b0011), .in4(4'b0100), .in5(4'b0101), .in6(4'b0110),
    .in7(4'b0111), .in8(4'b1000), .in9(4'b1001), .in10(4'b1010), .in11(4'b1011), .in12(4'b1100),
    .in13(4'b1101), .in14(4'b1110), .in15(4'b1111), .out(MS), .sel(in_1[7:4]));
  Multiplexer #(.select(4), .width(4)) multiplexer_2 (
    .in0(4'b0000), .in1(4'b0001), .in2(4'b0010), .in3(4'b0011), .in4(4'b0100), .in5(4'b0101), .in6(4'b0110),
    .in7(4'b0111), .in8(4'b1000), .in9(4'b1001), .in10(4'b1010), .in11(4'b1011), .in12(4'b1100),
    .in13(4'b1101), .in14(4'b1110), .in15(4'b1111), .out(LS), .sel(in_1[3:0]));
  Hex_Digit_Display hex_digit_display_1 (.value(MS));  // open: dp
  Hex_Digit_Display hex_digit_display_2 (.value(LS));  // open: dp
endmodule

module displayDec (
  input  [7:0] in_1,
  output A100,
  output B100,
  output C100,
  output D100,
  output E100,
  output F100,
  output G100,
  output A10,
  output B10,
  output C10,
  output D10,
  output E10,
  output F10,
  output G10,
  output A1,
  output B1,
  output C1,
  output D1,
  output E1,
  output F1,
  output G1
);

  wire binary_to_bcd_converter_1_p2, binary_to_bcd_converter_1_p3, binary_to_bcd_converter_1_p4;

  // Binary_to_BCD_converter #(.binvalue(8)) binary_to_bcd_converter_1: pin names not known; wires that end beside it: in_1, binary_to_bcd_converter_1_p2, binary_to_bcd_converter_1_p3, binary_to_bcd_converter_1_p4
  _7_Segment_Display #(.decimalPoint("false")) u_7_segment_display_1 (
    .g(G100), .f(F100), .a(A100), .b(B100), .e(E100), .d(D100), .c(C100));
  // BCD_to_7_Segment_decoder bcd_to_7_segment_decoder_1: pin names not known; wires that end beside it: G100, E100, F100, D100, binary_to_bcd_converter_1_p2, A100, C100, B100
  _7_Segment_Display #(.decimalPoint("false")) u_7_segment_display_2 (
    .g(G10), .f(F10), .a(A10), .b(B10), .e(E10), .d(D10), .c(C10));
  // BCD_to_7_Segment_decoder bcd_to_7_segment_decoder_2: pin names not known; wires that end beside it: G10, E10, F10, D10, binary_to_bcd_converter_1_p3, A10, C10, B10
  _7_Segment_Display #(.decimalPoint("false")) u_7_segment_display_3 (
    .g(G1), .f(F1), .a(A1), .b(B1), .e(E1), .d(D1), .c(C1));
  // BCD_to_7_Segment_decoder bcd_to_7_segment_decoder_3: pin names not known; wires that end beside it: G1, E1, F1, D1, binary_to_bcd_converter_1_p4, A1, C1, B1

  // Notes on the sheet:
  //   100
  //   10
  //   1
endmodule
